// Logisim project CPU_4bits_Final.circ as structural Verilog: 1 circuit, main circuit main
module main (
  input  [3:0] ENTRADA_A,
  input  [3:0] ENTRADA_B,
  output out_3
);

  wire and_1_out, and_2_out, and_3_out, and_4_out, and_5_out, and_6_out, and_7_out, and_8_out, clock_1_out,
       or_1_out, or_2_out, or_3_out, xor_1_out, xor_2_out, xor_3_out, xor_4_out, xor_5_out, xor_6_out,
       xor_7_out, xor_8_out;
  wire [3:0] counter_1_q, register_1_q, register_2_q, rom_1_data, xor_9_out;

  Counter #(.max('h1), .width(4)) counter_1 (
    .count(1'b1), .clk(clock_1_out), .Q(counter_1_q));  // open: clr, load, up, D, carry
  Clock clock_1 (.out(clock_1_out));
  ROM #(.addrWidth(4), .dataWidth(4), .misaligned("true")) rom_1 (.addr(counter_1_q), .data(rom_1_data));
  Register #(.width(4)) register_1 (.D(ENTRADA_A), .en(1'b1), .clk(clock_1_out), .Q(register_1_q));  // open: clr
  Register #(.width(4)) register_2 (.D(ENTRADA_B), .en(1'b1), .clk(clock_1_out), .Q(register_2_q));  // open: clr
  xor xor_1 (xor_1_out, register_2_q[0], rom_1_data[0]);
  xor xor_2 (xor_2_out, register_2_q[1], rom_1_data[0]);
  xor xor_3 (xor_3_out, register_2_q[2], rom_1_data[0]);
  xor xor_4 (xor_4_out, register_2_q[3], rom_1_data[0]);
  xor xor_5 (xor_5_out, register_1_q[0], xor_1_out);
  xor xor_6 (xor_6_out, register_1_q[1], xor_2_out);
  xor xor_7 (xor_7_out, register_1_q[2], xor_3_out);
  xor xor_8 (xor_8_out, register_1_q[3], xor_4_out);
  and and_1 (and_1_out, register_1_q[0], xor_1_out);
  and and_2 (and_2_out, register_1_q[1], xor_2_out);
  and and_3 (and_3_out, register_1_q[2], xor_3_out);
  and and_4 (and_4_out, register_1_q[3], xor_4_out);
  and and_5 (and_5_out, xor_5_out, rom_1_data[0]);
  and and_6 (and_6_out, xor_6_out, or_1_out);
  and and_7 (and_7_out, xor_7_out, or_2_out);
  and and_8 (and_8_out, xor_8_out, or_3_out);
  xor xor_9 (xor_9_out[0], xor_5_out, rom_1_data[0]);
  xor xor_10 (xor_9_out[1], xor_6_out, or_1_out);
  xor xor_11 (xor_9_out[2], xor_7_out, or_2_out);
  xor xor_12 (xor_9_out[3], xor_8_out, or_3_out);
  or or_1 (or_1_out, and_5_out, and_1_out);
  or or_2 (or_2_out, and_6_out, and_2_out);
  or or_3 (or_3_out, and_7_out, and_3_out);
  or or_4 (out_3, and_8_out, and_4_out);
  Hex_Digit_Display hex_digit_display_1 (.value(xor_9_out));  // open: dp
  LED led_1 (.in(xor_9_out[3]));
  LED led_2 (.in(xor_9_out[2]));
  LED led_3 (.in(xor_9_out[1]));
  LED led_4 (.in(xor_9_out[0]));

  // Notes on the sheet:
  //   CONSTANTE 1
  //   RELOJ
  //   CONTADOR
  //   HABILITAR = 1
  //   UNIDAD DE CONTROL
  //   ENTRADA DE DIRECCIÓN
  //   contents of rom_1 (hex, n*v repeats v):
  //   0 1
  //   MEMORIA ROM
  //   BANCO DE REGISTROS
  //   REGISTRO A
  //   REGISTRO B
  //   ADD/SUB
  //   CARRY INICIAL
  //   UNIDAD ARITMÉTICO LÓGICA (ALU)
  //   ACARREO DE SALIDA
  //   RESULTADO DECIMAL
  //   SALIDA
  //   RESULTADO BINARIO
endmodule
